# Fritzing sketch arduino_slave (saved by Fritzing 0.7.12b)
breadboards: 1

parts:
  Part1 = Logic Level Converter
  Arduino1 = Arduino
  Part2 = Electric Imp Breakout

nets:
  N1: Part1.TX2_LV, Part2.4
  N2: Part1.RX2_LV, Part2.3
  GND: Part1.GND, Arduino1.GND, Part2.11
  N3: Part1.LV, Part2.8
  N4: Part1.HV, Arduino1.+5V
  N5: Part1.RX2_HV, Arduino1.D0RX
  N6: Part1.TX2_HV, Arduino1.D1TX
  N7: Part2.13, Part2.14

notes:
  Don't forget to short the USB jumper on the Imp Breakout

custom parts:
  Electric Imp Breakout: Electric Imp Breakout Board with onboard 3.3V regulated power supply
